# Fritzing sketch battery sketch (saved by Fritzing 0.9.3b)
breadboards: 1

parts:
  Raspberry_Pi_Zero1 = Raspberry Pi Zero
  Part1 = PowerBoost 500 Charger
  U1 = LIPO-2000mAh [package=lipo-2000]
  SparkFun_LiPo_Fuel_Gauge1 = SparkFun LiPo Fuel Gauge [part_number=TOL-10617]

nets:
  N1: Raspberry_Pi_Zero1.GPIO2, SparkFun_LiPo_Fuel_Gauge1.SDA
  N2: Raspberry_Pi_Zero1.GPIO3, SparkFun_LiPo_Fuel_Gauge1.SCL
  GND: Raspberry_Pi_Zero1.GND, Part1.GND_BAT_IN, U1.-, SparkFun_LiPo_Fuel_Gauge1.GND
  N3: Part1.VBAT_IN, U1.+, SparkFun_LiPo_Fuel_Gauge1.VCC

custom parts:
  SparkFun LiPo Fuel Gauge: LiPo batteries are a great way to power your projects. They’re small, lightweight, and pack a pretty good punch for their size. Unfortunately, even the best batteries eventually run low on power and when they do it’s often unexpected (and at the worst time). Don’t be caught by surprise next time your board suddenly powers-down! The SparkFun LiPo Fuel Gauge connects your battery to your project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
